# Fritzing sketch circuit (saved by Fritzing 0.9.2b)
breadboards: 1

parts:
  R1 = Resistor [tolerance=±5% resistance=10k package=THT]
  R2 = Resistor [tolerance=±5% resistance=10k package=THT]
  R3 = Resistor [tolerance=±5% resistance=10k package=THT]
  R4 = Resistor [tolerance=±5% resistance=10k package=THT]
  R5 = Resistor [tolerance=±5% resistance=10k package=THT]
  R6 = Resistor [tolerance=±5% resistance=10k package=THT]
  R7 = Resistor [tolerance=±5% resistance=10k package=THT]
  LED1 = LED - 3mm [color="Red (633nm)" package="3 mm [THT]"]
  LED2 = LED - 3mm [color="Red (633nm)" package="3 mm [THT]"]
  LED3 = LED - 3mm [color="Red (633nm)" package="3 mm [THT]"]
  LED4 = LED - 3mm [color="Red (633nm)" package="3 mm [THT]"]
  LED5 = LED - 3mm [color="Red (633nm)" package="3 mm [THT]"]
  LED6 = LED - 3mm [color="Red (633nm)" package="3 mm [THT]"]
  LED7 = LED - 3mm [color="Red (633nm)" package="3 mm [THT]"]
  Part1 = Arduino Uno (Rev3)

nets:
  N1: R1.Pin_0, LED2.anode
  N2: R1.Pin_1, Part1.D2
  N3: R2.Pin_0, LED1.anode
  N4: R2.Pin_1, Part1.D3_PWM
  N5: R3.Pin_0, LED3.anode
  N6: R3.Pin_1, Part1.D4
  N7: R4.Pin_0, LED4.anode
  N8: R4.Pin_1, Part1.D5_PWM
  N9: R5.Pin_0, LED6.anode
  N10: R5.Pin_1, Part1.D7
  N11: R6.Pin_0, LED5.anode
  N12: R6.Pin_1, Part1.D6_PWM
  N13: R7.Pin_0, LED7.anode
  N14: R7.Pin_1, Part1.D8
  N15: LED1.cathode, LED2.cathode, LED3.cathode, LED4.cathode, LED5.cathode, LED6.cathode, LED7.cathode, Part1.D9_PWM
